# Fritzing sketch acq_2 (saved by Fritzing 0.9.3b)
breadboards: 1

parts:
  U1 = ESP32-38PinWide [part_number=ESP32-38PinWide]
  S1 = Toggle Switch [package=THT]
  S2 = Toggle Switch [package=THT]
  DHT1 = DHT11 Humitidy and Temperature Sensor
  U2 = 4-Channel 5v Relay Shield [package=relay-4ch5v10a]
  DS1 = DS18B20 1-Wire Temperature Sensor [part_number=DS18B20]

nets:
  VDD: U1.3.3, DHT1.VDD, DS1.VDD
  N1: U1.GPIO25, U2.IN4
  N2: U1.GPIO26, U2.IN3
  N3: U1.GPIO27, U2.IN2
  N4: U1.GPIO14, U2.IN1
  GND: U1.GND, S1.L1, S2.L1, DHT1.GND, U2.GND, DS1.GND
  VIN: U1.VIN, U2.VCC
  N5: U1.GPIO15, DHT1.DATA
  N6: U1.GPIO2, DS1.DQ
  N7: U1.GPIO19, S2.COM
  N8: U1.GPIO23, S1.COM, S1.L2

notes:
  water level sensor x2
  water temperature
  refill pump
  Fan
  Lamp1
  Lamp2
  Environment temperature

custom parts:
  ESP32-38PinWide: Generic 38-Pin ESP32 with wide format (only access to one side of pins on a breadboard) based on Stephen Lilley's HiLetgo ESP-WROOM-32 ESP32 ESP-32S Development Board.
  DHT11 Humitidy and Temperature Sensor: DHT11 Humidity and Temperature Sensor
  4-Channel 5v Relay Shield: 4 Channel 5v Relay Shield w. 2x SPD-06VDC-SD-C
